# Fritzing sketch Devreler (saved by Fritzing 0.9.9b)
perfboards: 1

parts:
  Part1 = Arduino Pro Micro (Clone)  # not connected
  Part2 = Arduino Micro (Rev3)
  Part3 = NRF24L01+ Breakout Board
  Part4 = InvenSense MPU6050
  Part5 = Arduino Pro Micro (Clone)
  Part6 = NRF24L01+ Breakout Board
  Part7 = NRF24L01+ Breakout Board  # not connected
  R3 = Resistor [tolerance=±5% resistance=100k power=0.25 package=THT]
  R4 = Resistor [tolerance=±5% resistance=100k power=0.25 package=THT]
  R5 = Resistor [tolerance=±5% resistance=100k power=0.25 package=THT]
  R6 = Resistor [tolerance=±5% resistance=100k power=0.25 package=THT]
  R7 = Resistor [tolerance=±5% resistance=100k power=0.25 package=THT]
  R8 = Resistor [tolerance=±5% resistance=100k power=0.25 package=THT]
  R9 = Resistor [tolerance=±5% resistance=100k power=0.25 package=THT]
  R10 = Resistor [tolerance=±5% resistance=100k power=0.25 package=THT]
  R11 = Resistor [tolerance=±5% resistance=100k power=0.25 package=THT]
  R12 = Resistor [tolerance=±5% resistance=100k power=0.25 package=THT]
  R13 = Resistor [tolerance=±5% resistance=100k power=0.25 package=THT]
  R14 = Resistor [tolerance=±5% resistance=100k power=0.25 package=THT]
  R15 = Resistor [tolerance=±5% resistance=100k power=0.25 package=THT]
  R16 = Resistor [tolerance=±5% resistance=100k power=0.25 package=THT]
  R17 = Resistor [tolerance=±5% resistance=100k power=0.25 package=THT]

nets:
  N1: Part2.MOSI, Part3.MOSI
  GND: Part2.GND, Part3.GND, Part4.GND
  N2: Part2.D2/SDA, Part4.SDA
  N3: Part2.D3/SCL, Part4.SCL
  N4: Part2.D4_PWM/A6, R3.Pin_0, R4.Pin_0, R5.Pin_0, R6.Pin_0, R7.Pin_0, R8.Pin_0, R9.Pin_0, R10.Pin_0, R11.Pin_0, R12.Pin_0, R13.Pin_0, R14.Pin_0, R15.Pin_0, R16.Pin_0, R17.Pin_0
  N5: Part2.D7, Part3.CS
  N6: Part2.D8_PWM/A8, Part3.CE
  N7: Part2.SCK, Part3.SCK
  N8: Part2.MISO, Part3.MISO
  5V: Part2.5V, Part4.VCC
  3V3: Part2.3V3, Part3.VCC
  GND_2: Part5.GND, Part6.GND
  N9: Part5.D7, Part6.CE
  N10: Part5.D8, Part6.CS
  N11: Part5.D16, Part6.MOSI
  N12: Part5.D14, Part6.MISO
  N13: Part5.D15, Part6.SCK
  VCC: Part5.VCC, Part6.VCC
