# Fritzing sketch Globe-Trotter (saved by Fritzing 0.9.9b)
circuit board: 8.46667cm x 5.64444cm
breadboards: 1

parts:
  Arduino_Micro = Arduino Micro (Rev3)
  R1 = Resistor [tolerance=±5% resistance=100k power=0.25 package=THT]
  R2 = Resistor [tolerance=±5% resistance=100k power=0.25 package=THT]
  C1 = Ceramic Capacitor [capacitance=0.1µF voltage=35V package="100 mil [THT, multilayer]"]
  C2 = Ceramic Capacitor [capacitance=0.1µF package="100 mil [THT, multilayer]"]
  RobotDyn_Rotary_Encoder = IC, SIP package, 4 pins [chip_label="Rotary encoder"]

nets:
  N1: Arduino_Micro.GND, C1.0, C2.0, RobotDyn_Rotary_Encoder.pin2
  N2: Arduino_Micro.D2/SDA, C2.1, RobotDyn_Rotary_Encoder.pin3
  N3: Arduino_Micro.D3/SCL, C1.1, RobotDyn_Rotary_Encoder.pin4
  N4: Arduino_Micro.D4_PWM/A6, R1.Pin_1, R2.Pin_1
  N5: Arduino_Micro.D5_PWM, R1.Pin_0
  N6: Arduino_Micro.D6_PWM/A7, R2.Pin_0
  N7: Arduino_Micro.5V, RobotDyn_Rotary_Encoder.pin1

notes:
  country 1
  country 2
  send pin
  receive pin
